# Fritzing sketch camera-control-breakout (saved by Fritzing 0.9.9b)
perfboards: 1

parts:
  Q1 = NPN-Transistor [package="TO92 [THT]"]
  JL = female pin header, 2 pins [form="♀ (female)"]
  R1 = Resistor [tolerance=±5% power=0.25 resistance=120 package=THT]
  Jpan = male pin header, 3 pins [form="♂ (male)"]
  Jtilt = male pin header, 3 pins [form="♂ (male)"]
  Jin = female pin header, 6 pins [form="♀ (female)"]

nets:
  GND: Q1.E, Jpan.pin3, Jtilt.pin3, Jin.pin6
  N1: Q1.B, R1.Pin_1
  N2: Q1.C, JL.pin2
  3.3V: JL.pin1, Jin.pin2
  N3: R1.Pin_0, Jin.pin3
  Pan: Jpan.pin1, Jin.pin4
  5V: Jpan.pin2, Jtilt.pin2, Jin.pin1
  Tilt: Jtilt.pin1, Jin.pin5

notes:
  Use L-shaped male headers
